# Fritzing sketch LCD 2 (saved by Fritzing 0.9.4)
breadboards: 2

parts:
  Arduino(UNO)1 = Arduino Uno (Rev3) - ICSP
  LCD1 = 128 x 64 Graphic LCD
  R2 = Rotary Potentiometer (Large) [maximum_resistance=100kΩ package=THT]
  R3 = Rotary Potentiometer (Large) [maximum_resistance=100kΩ package=THT]
  R4 = Rotary Potentiometer (Large) [maximum_resistance=100kΩ package=THT]

nets:
  N1: Arduino(UNO)1.A0, R4.wiper
  N2: Arduino(UNO)1.A1, R3.wiper
  N3: Arduino(UNO)1.GND, LCD1.2_Vdd, LCD1.15_CS1, LCD1.20_K(-), R2.leg2, R3.leg1, R4.leg1
  N4: Arduino(UNO)1.D10_PWM/SS, LCD1.4_D/I
  N5: Arduino(UNO)1.D11_PWM/MOSI, LCD1.5_R/W
  N6: Arduino(UNO)1.D13/SCK, LCD1.6_Enable
  N7: Arduino(UNO)1.5V, LCD1.1_Vss, LCD1.19_A(+), R3.leg2, R4.leg2
  N8: LCD1.3_Vo, R2.wiper
  N9: LCD1.18_Vout, R2.leg1
