# Fritzing sketch LCD (saved by Fritzing 0.9.4)
breadboards: 1

parts:
  LCD = 128 x 64 Graphic LCD
  R1 = Rotary Potentiometer (Large) [maximum_resistance=100kΩ package=THT]
  Arduino(UNO) = Arduino Uno (Rev3) - ICSP

nets:
  N1: LCD.1_Vss, LCD.19_A(+), Arduino(UNO).5V
  N2: LCD.2_Vdd, LCD.15_CS1, LCD.20_K(-), R1.leg2, Arduino(UNO).GND
  N3: LCD.3_Vo, R1.wiper
  N4: LCD.4_D/I, Arduino(UNO).D10_PWM/SS
  N5: LCD.5_R/W, Arduino(UNO).D11_PWM/MOSI
  N6: LCD.6_Enable, Arduino(UNO).D13/SCK
  N7: LCD.18_Vout, R1.leg1
