# Fritzing sketch main (saved by Fritzing 0.9.4)
breadboards: 1

parts:
  Arduino(UNO)1 = Arduino Uno (Rev3) - ICSP
  LCD1 = 128 x 64 Graphic LCD
  R2 = Rotary Potentiometer (Large) [maximum_resistance=100kΩ package=THT]
  R3 = Resistor [tolerance=±5% resistance=220 package=THT]
  S1 = Pushbutton [package="[THT]"]

nets:
  N1: Arduino(UNO)1.5V, LCD1.1_Vss, LCD1.19_A(+), S1.Pin_3
  N2: Arduino(UNO)1.GND, LCD1.2_Vdd, LCD1.15_CS1, LCD1.20_K(-), R2.leg2, R3.Pin_0
  N3: Arduino(UNO)1.D8, R3.Pin_1, S1.Pin_1
  N4: Arduino(UNO)1.D10_PWM/SS, LCD1.4_D/I
  N5: Arduino(UNO)1.D11_PWM/MOSI, LCD1.5_R/W
  N6: Arduino(UNO)1.D13/SCK, LCD1.6_Enable
  N7: LCD1.3_Vo, R2.wiper
  N8: LCD1.18_Vout, R2.leg1
